# Fritzing sketch capreravr (saved by Fritzing 0.9.3b)
breadboards: 1

parts:
  Part1 = Arduino Uno (Rev3)
  DFRobot-DFPlayer-Mini1 = DFRobot-DFPlayer-Mini [part_number=DFR0299]
  R1 = Resistor [tolerance=±5% resistance=1k package=THT]
  R2 = Resistor [tolerance=±5% resistance=1k package=THT]
  SP1 = SPEAKER [package=pcb_mount_speaker]
  R3 = Resistor [tolerance=±5% resistance=10k package=THT]
  C1 = Ceramic Capacitor [capacitance=100nF package="100 mil [THT, multilayer]"]
  S1 = Round Pushbutton

nets:
  N1: Part1.D0/RX, R2.Pin_1
  N2: Part1.D1/TX, R1.Pin_1
  N3: Part1.D2, R3.Pin_0, C1.1, S1.leg1
  5V: Part1.5V, DFRobot-DFPlayer-Mini1.VCC, C1.0, S1.leg0
  N4: Part1.GND, DFRobot-DFPlayer-Mini1.GND-1, DFRobot-DFPlayer-Mini1.GND-2, R3.Pin_1
  N5: DFRobot-DFPlayer-Mini1.RX, R1.Pin_0
  N6: DFRobot-DFPlayer-Mini1.TX, R2.Pin_0
  N7: DFRobot-DFPlayer-Mini1.SPK_1, SP1.-
  N8: DFRobot-DFPlayer-Mini1.SPK_2, SP1.+
